// Logisim project circuit.circ as structural Verilog: 2 circuits, main circuit main
// dec
module main (
  input  [3:0] in_1,
  input  in_2,
  input  [1:0] FUNSEL,
  output [3:0] out_4
);

  wire clock_1_out, decoder_1_out0, decoder_1_out1;

  Clock clock_1 (.out(clock_1_out));
  Decoder #(.select(2)) decoder_1 (
    .out0(decoder_1_out0), .out1(decoder_1_out1), .sel(FUNSEL), .en(in_2));  // open: out2, out3
  D_Flip_Flop d_ff_1 (
    .clk(clock_1_out), .D(in_1[3]), .Q(out_4[3]), .en(decoder_1_out1), .reset(decoder_1_out0));  // open: Qn, preset
  D_Flip_Flop d_ff_2 (
    .clk(clock_1_out), .D(in_1[2]), .Q(out_4[2]), .en(decoder_1_out1), .reset(decoder_1_out0));  // open: Qn, preset
  D_Flip_Flop d_ff_3 (
    .clk(clock_1_out), .D(in_1[1]), .Q(out_4[1]), .en(decoder_1_out1), .reset(decoder_1_out0));  // open: Qn, preset
  D_Flip_Flop d_ff_4 (
    .clk(clock_1_out), .D(in_1[0]), .Q(out_4[0]), .en(decoder_1_out1), .reset(decoder_1_out0));  // open: Qn, preset
endmodule

module incr (
  input  in_1,
  output [2:0] out_2
);

  wire and_1_out, clock_1_out, not_1_out, xor_1_out, xor_2_out;

  Clock clock_1 (.out(clock_1_out));
  xor xor_1 (xor_1_out, and_1_out, out_2[2]);
  D_Flip_Flop d_ff_1 (.clk(clock_1_out), .D(xor_1_out), .Q(out_2[2]), .en(in_1));  // open: Qn, preset, reset
  D_Flip_Flop d_ff_2 (.clk(clock_1_out), .D(xor_2_out), .Q(out_2[1]), .en(in_1));  // open: Qn, preset, reset
  xor xor_2 (xor_2_out, out_2[1], out_2[0]);
  not not_1 (not_1_out, out_2[0]);
  and and_1 (and_1_out, out_2[1], out_2[0]);
  D_Flip_Flop d_ff_3 (.clk(clock_1_out), .D(not_1_out), .Q(out_2[0]), .en(in_1));  // open: Qn, preset, reset
endmodule
